# Fritzing sketch with_Arduino (saved by Fritzing 0.9.3b)

parts:
  PCD = RFID-RC522-v2
  Uno = Arduino Uno (Rev3) - ICSP

nets:
  N1: PCD.SDA, Uno.D10_PWM/SS
  N2: PCD.SCK, Uno.D13/SCK
  N3: PCD.MOSI, Uno.D11_PWM/MOSI
  N4: PCD.MISO, Uno.D12/MISO
  GND: PCD.GND, Uno.GND
  N5: PCD.RST, Uno.D9_PWM
  3.3V: PCD.3.3V, Uno.3V3

notes:
  __________________________________________________________________
  | UNO | PCD |
  |============================================== =|
  | 3V3 | 3.3V |
  | GND | GND |
  | D9 | RST |
  | D10 | SDA |
  | D11 | MISO |
  | D12 | MOSI |
  | D13 | SCK |
  |______________________________________________________________ _|

custom parts:
  RFID-RC522-v2: A simple China made RFID-RC522 Reader; do check the pin labels, as this is a MFRC522 based clone.
