# Fritzing sketch with_NodeMCU (saved by Fritzing 0.9.3b)

parts:
  NodeMCU = NodeMCU V1.0
  PCD = RFID-RC522-v2

nets:
  N1: NodeMCU.D1, PCD.RST
  N2: NodeMCU.D2, PCD.SDA
  3V3: NodeMCU.3V3, PCD.3.3V
  GND: NodeMCU.GND, PCD.GND
  N3: NodeMCU.D5, PCD.SCK
  N4: NodeMCU.D6, PCD.MISO
  N5: NodeMCU.D7, PCD.MOSI

notes:
  __________________________________________________________________
  | NodeMCU | PCD |
  |============================================== =|
  | 3V3 | 3.3V |
  | GND | GND |
  | D1 | RST |
  | D2 | SDA |
  | D7 | MISO |
  | D6 | MOSI |
  | D5 | SCK |
  |______________________________________________________________ _|

custom parts:
  NodeMCU V1.0: ESP8266 based NodeMCU
  RFID-RC522-v2: A simple China made RFID-RC522 Reader; do check the pin labels, as this is a MFRC522 based clone.
